// Logisim project mehedi_2107086.circ as structural Verilog
module circuitimp (
  input  Clock_Pulse_80dce73d,
  output clk_out_5556a344,
  output rc,
  output rb,
  output ra,
  output r0,
  output lb,
  output la,
  output l0
);

  wire and_2_out, and_3_out, and_4_out, and_5_out, and_6_out, and_7_out, j_k_ff_4_qn, j_k_ff_7_q, not_1_out,
       not_2_out, undriven;

  and and_1 (clk_out_5556a344, l0, la, lb);
  J_K_Flip_Flop j_k_ff_1 (.J(1'b1), .clk(l0), .K(1'b1), .Q(l0), .Qn(l0));  // open: preset, reset
  and and_2 (and_2_out, l0, lb);
  J_K_Flip_Flop j_k_ff_2 (.clk(l0), .Q(l0), .Qn(l0), .preset(la));  // open: J, K, reset
  and and_3 (and_3_out, l0, la);
  J_K_Flip_Flop j_k_ff_3 (.J(and_3_out), .clk(l0), .K(l0), .Q(lb), .Qn(lb));  // open: preset, reset
  nand nand_1 (l0, rc, not_1_out, not_2_out, r0);
  and and_4 (and_4_out, l0, la, lb, j_k_ff_7_q, rb, undriven, j_k_ff_4_qn);
  not not_1 (not_1_out, rb);
  not not_2 (not_2_out, ra);
  J_K_Flip_Flop j_k_ff_4 (
    .J(1'b1), .clk(Clock_Pulse_80dce73d), .K(1'b1), .Q(r0), .Qn(j_k_ff_4_qn), .preset(and_4_out));  // open: reset
  and and_5 (and_5_out, r0, j_k_ff_7_q);
  J_K_Flip_Flop j_k_ff_5 (.K(and_4_out), .clk(and_4_out), .preset(ra), .reset(and_4_out));  // open: J, Q, Qn
  and and_6 (and_6_out, ra, r0);
  J_K_Flip_Flop j_k_ff_6 (.K(and_4_out), .clk(and_4_out), .Q(r0), .preset(rb), .reset(and_4_out));  // open: J, Qn
  and and_7 (and_7_out, rb, and_6_out);
  J_K_Flip_Flop j_k_ff_7 (
    .K(and_4_out), .clk(and_4_out), .Q(j_k_ff_7_q), .preset(rc), .reset(and_4_out));  // open: J, Qn

  // Notes on the sheet:
  //   2107086
endmodule
