// Logisim project new_Mehedi_2107086.circ as structural Verilog: 10 circuits, main circuit main
module main (
);

  wire button_1_out, clock_1_out, clockanalysisdecoding_1_clk_out, clockanalysisdecoding_1_mia,
       clockanalysisdecoding_1_mib, clockanalysisdecoding_1_mic, clockanalysisdecoding_1_mid,
       clockanalysisdecoding_1_mie, clockanalysisdecoding_1_mif, clockanalysisdecoding_1_mig,
       clockanalysisdecoding_1_msa, clockanalysisdecoding_1_msb, clockanalysisdecoding_1_msc,
       clockanalysisdecoding_1_msd, clockanalysisdecoding_1_mse, clockanalysisdecoding_1_msf,
       clockanalysisdecoding_1_msg, clockanalysisdecoding_1_sia, clockanalysisdecoding_1_sib,
       clockanalysisdecoding_1_sic, clockanalysisdecoding_1_sid, clockanalysisdecoding_1_sie,
       clockanalysisdecoding_1_sif, clockanalysisdecoding_1_sig, clockanalysisdecoding_1_ssa,
       clockanalysisdecoding_1_ssb, clockanalysisdecoding_1_ssc, clockanalysisdecoding_1_ssd,
       clockanalysisdecoding_1_sse, clockanalysisdecoding_1_ssf, clockanalysisdecoding_1_ssg,
       l_1t012counter_1b653834_1_am_pm_b337f7e9, l_1t012counter_1b653834_1_q0, l_1t012counter_1b653834_1_q1,
       l_1t012counter_1b653834_1_q2, l_1t012counter_1b653834_1_q3, simplify_1_qa0, simplify_1_qanot_89345d3a,
       simplify_1_qb0, simplify_1_qb1, simplify_1_qc0, simplify_1_qc1, simplify_1_qd0, simplify_1_qd1,
       simplify_1_qe0, simplify_1_qenot_3fae106c, simplify_1_qf0, simplify_1_qfnot_432cf589, simplify_1_qg0,
       simplify_1_qg1, xor_1_out;

  _7_Segment_Display u_7_segment_display_1 (
    .g(clockanalysisdecoding_1_mig), .f(clockanalysisdecoding_1_mif), .a(clockanalysisdecoding_1_mia),
    .b(clockanalysisdecoding_1_mib), .e(clockanalysisdecoding_1_mie), .d(clockanalysisdecoding_1_mid),
    .c(clockanalysisdecoding_1_mic));  // open: dp
  _7_Segment_Display u_7_segment_display_2 (
    .g(clockanalysisdecoding_1_msg), .f(clockanalysisdecoding_1_msf), .a(clockanalysisdecoding_1_msa),
    .b(clockanalysisdecoding_1_msb), .e(clockanalysisdecoding_1_mse), .d(clockanalysisdecoding_1_msd),
    .c(clockanalysisdecoding_1_msc));  // open: dp
  _7_Segment_Display u_7_segment_display_3 (
    .g(simplify_1_qg1), .f(simplify_1_qfnot_432cf589), .a(simplify_1_qanot_89345d3a), .b(simplify_1_qb1),
    .e(simplify_1_qenot_3fae106c), .d(simplify_1_qd1), .c(simplify_1_qc1));  // open: dp
  _7_Segment_Display u_7_segment_display_4 (
    .g(simplify_1_qg0), .f(simplify_1_qf0), .a(simplify_1_qa0), .b(simplify_1_qb0), .e(simplify_1_qe0),
    .d(simplify_1_qd0), .c(simplify_1_qc0));  // open: dp
  Clockanalysisdecoding clockanalysisdecoding_1 (
    .Clock_Pulse(clock_1_out), .clk_out(clockanalysisdecoding_1_clk_out), .sia(clockanalysisdecoding_1_sia),
    .ssa(clockanalysisdecoding_1_ssa), .Sib(clockanalysisdecoding_1_sib), .ssb(clockanalysisdecoding_1_ssb),
    .Mia(clockanalysisdecoding_1_mia), .Msa(clockanalysisdecoding_1_msa), .Sic(clockanalysisdecoding_1_sic),
    .ssc(clockanalysisdecoding_1_ssc), .Mib(clockanalysisdecoding_1_mib), .Msb(clockanalysisdecoding_1_msb),
    .Mic(clockanalysisdecoding_1_mic), .Msc(clockanalysisdecoding_1_msc), .Sid(clockanalysisdecoding_1_sid),
    .ssd(clockanalysisdecoding_1_ssd), .Mid(clockanalysisdecoding_1_mid), .Msd(clockanalysisdecoding_1_msd),
    .sie(clockanalysisdecoding_1_sie), .sse(clockanalysisdecoding_1_sse), .sif(clockanalysisdecoding_1_sif),
    .ssf(clockanalysisdecoding_1_ssf), .Mie(clockanalysisdecoding_1_mie), .Mse(clockanalysisdecoding_1_mse),
    .sig(clockanalysisdecoding_1_sig), .ssg(clockanalysisdecoding_1_ssg), .Mif(clockanalysisdecoding_1_mif),
    .Msf(clockanalysisdecoding_1_msf), .Mig(clockanalysisdecoding_1_mig), .Msg(clockanalysisdecoding_1_msg));
  _7_Segment_Display u_7_segment_display_5 (
    .g(clockanalysisdecoding_1_sig), .f(clockanalysisdecoding_1_sif), .a(clockanalysisdecoding_1_sia),
    .b(clockanalysisdecoding_1_sib), .e(clockanalysisdecoding_1_sie), .d(clockanalysisdecoding_1_sid),
    .c(clockanalysisdecoding_1_sic));  // open: dp
  Clock clock_1 (.out(clock_1_out));
  _7_Segment_Display u_7_segment_display_6 (
    .g(clockanalysisdecoding_1_ssg), .f(clockanalysisdecoding_1_ssf), .a(clockanalysisdecoding_1_ssa),
    .b(clockanalysisdecoding_1_ssb), .e(clockanalysisdecoding_1_sse), .d(clockanalysisdecoding_1_ssd),
    .c(clockanalysisdecoding_1_ssc));  // open: dp
  Button button_1 (.out(button_1_out));
  xor xor_1 (xor_1_out, button_1_out, clockanalysisdecoding_1_clk_out);
  LED PM (.in(l_1t012counter_1b653834_1_am_pm_b337f7e9));
  L_1t012counter_1b653834 l_1t012counter_1b653834_1 (
    .am_pm_b337f7e9(l_1t012counter_1b653834_1_am_pm_b337f7e9), .Q3(l_1t012counter_1b653834_1_q3),
    .Q2(l_1t012counter_1b653834_1_q2), .Q1(l_1t012counter_1b653834_1_q1), .Q0(l_1t012counter_1b653834_1_q0),
    .Clk_In_f31b25c5(xor_1_out));
  simplify simplify_1 (
    .I3(l_1t012counter_1b653834_1_q3), .I2(l_1t012counter_1b653834_1_q2), .I1(l_1t012counter_1b653834_1_q1),
    .I0(l_1t012counter_1b653834_1_q0), .QANOT_89345d3a(simplify_1_qanot_89345d3a), .QB1(simplify_1_qb1),
    .QD1(simplify_1_qd1), .QENOT_3fae106c(simplify_1_qenot_3fae106c), .QC1(simplify_1_qc1),
    .QFNOT_432cf589(simplify_1_qfnot_432cf589), .QG1(simplify_1_qg1), .QA0(simplify_1_qa0),
    .QB0(simplify_1_qb0), .QC0(simplify_1_qc0), .QD0(simplify_1_qd0), .QE0(simplify_1_qe0),
    .QF0(simplify_1_qf0), .QG0(simplify_1_qg0));

  // Notes on the sheet:
  //   2107086
endmodule

module sevensegment_BCDto_dd79e25d (
  input  in_1,
  input  in_2,
  input  D,
  input  in_4,
  output a,
  output b,
  output c,
  output out_8,
  output e,
  output f,
  output g
);

  wire and_1_out, and_2_out, and_3_out, and_4_out, and_5_out, and_6_out, and_7_out, and_8_out, and_9_out,
       not_1_out, not_2_out, not_3_out, or_1_out, or_2_out, or_4_out, or_5_out, or_6_out, or_7_out, or_8_out,
       or_10_out, or_14_out;

  not not_1 (not_1_out, in_4);
  not not_2 (not_2_out, in_2);
  not not_3 (not_3_out, D);
  and and_1 (and_1_out, in_2, D);
  and and_2 (and_2_out, and_1_out, not_1_out);
  and and_3 (and_3_out, in_2, not_1_out);
  and and_4 (and_4_out, in_4, not_2_out);
  and and_5 (and_5_out, not_1_out, not_3_out);
  and and_6 (and_6_out, not_2_out, not_3_out);
  and and_7 (and_7_out, in_4, not_3_out);
  and and_8 (and_8_out, in_2, not_3_out);
  and and_9 (and_9_out, in_4, D);
  or or_1 (or_1_out, in_1, in_4);
  or or_2 (or_2_out, in_1, not_2_out);
  or or_3 (e, and_6_out, and_7_out);
  or or_4 (or_4_out, in_1, and_3_out);
  or or_5 (or_5_out, and_6_out, and_1_out);
  or or_6 (or_6_out, and_5_out, and_9_out);
  or or_7 (or_7_out, in_2, not_1_out);
  or or_8 (or_8_out, in_1, and_4_out);
  or or_9 (b, or_2_out, or_6_out);
  or or_10 (or_10_out, or_4_out, and_8_out);
  or or_11 (g, or_10_out, and_4_out);
  or or_12 (a, or_1_out, or_5_out);
  or or_13 (c, or_7_out, D);
  or or_14 (or_14_out, or_8_out, e);
  or or_15 (out_8, or_14_out, and_2_out);
  or or_16 (f, or_10_out, and_5_out);
  _7_Segment_Display u_7_segment_display_1 (.g(g), .f(f), .a(a), .b(b), .e(e), .d(out_8), .c(c));  // open: dp

  // Notes on the sheet:
  //   2107086
endmodule

module minutessecondscombination (
  input  Clock_Pluse,
  output si0,
  output clk_out,
  output si1,
  output si2,
  output si3,
  output Sl0,
  output sl1,
  output ml2,
  output ml1,
  output ml0,
  output mi3,
  output mi2,
  output mi1,
  output mi0,
  output sl2
);

  wire nand_1_out, not_1_out, not_2_out, not_3_out;

  nand nand_1 (nand_1_out, sl2, not_1_out, Sl0, si3, not_2_out, not_3_out, si0);
  Circuitmostimportant circuitmostimportant_1 (
    .Clock_Pulse_5c32f6d8(Clock_Pluse), .lb(sl2), .la(sl1), .l0(Sl0), .rc(si3), .rb(si2), .ra(si1), .r0(si0));  // open: clk_out_9ee9bf02
  not not_1 (not_1_out, sl1);
  not not_2 (not_2_out, si2);
  not not_3 (not_3_out, si1);
  Circuitmostimportant circuitmostimportant_2 (
    .Clock_Pulse_5c32f6d8(nand_1_out), .lb(ml2), .la(ml1), .l0(ml0), .rc(mi3), .rb(mi2), .ra(mi1), .r0(mi0),
    .clk_out_9ee9bf02(clk_out));

  // Notes on the sheet:
  //   2107086
endmodule

module Circuitmostimportant (
  input  Clock_Pulse_5c32f6d8,
  output clk_out_9ee9bf02,
  output rc,
  output rb,
  output ra,
  output r0,
  output lb,
  output la,
  output l0
);

  wire and_2_out, and_3_out, and_4_out, and_5_out, and_6_out, and_7_out, j_k_ff_4_qn, j_k_ff_7_q, not_1_out,
       not_2_out, undriven;

  and and_1 (clk_out_9ee9bf02, l0, la, lb);
  J_K_Flip_Flop j_k_ff_1 (.J(1'b1), .clk(l0), .K(1'b1), .Q(l0), .Qn(l0));  // open: preset, reset
  and and_2 (and_2_out, l0, lb);
  J_K_Flip_Flop j_k_ff_2 (.clk(l0), .Q(l0), .Qn(l0), .preset(la));  // open: J, K, reset
  and and_3 (and_3_out, l0, la);
  J_K_Flip_Flop j_k_ff_3 (.J(and_3_out), .clk(l0), .K(l0), .Q(lb), .Qn(lb));  // open: preset, reset
  nand nand_1 (l0, rc, not_1_out, not_2_out, r0);
  and and_4 (and_4_out, l0, la, lb, j_k_ff_7_q, rb, undriven, j_k_ff_4_qn);
  not not_1 (not_1_out, rb);
  not not_2 (not_2_out, ra);
  J_K_Flip_Flop j_k_ff_4 (
    .J(1'b1), .clk(Clock_Pulse_5c32f6d8), .K(1'b1), .Q(r0), .Qn(j_k_ff_4_qn), .preset(and_4_out));  // open: reset
  and and_5 (and_5_out, r0, j_k_ff_7_q);
  J_K_Flip_Flop j_k_ff_5 (.K(and_4_out), .clk(and_4_out), .preset(ra), .reset(and_4_out));  // open: J, Q, Qn
  and and_6 (and_6_out, ra, r0);
  J_K_Flip_Flop j_k_ff_6 (.K(and_4_out), .clk(and_4_out), .Q(r0), .preset(rb), .reset(and_4_out));  // open: J, Qn
  and and_7 (and_7_out, rb, and_6_out);
  J_K_Flip_Flop j_k_ff_7 (
    .K(and_4_out), .clk(and_4_out), .Q(j_k_ff_7_q), .preset(rc), .reset(and_4_out));  // open: J, Qn

  // Notes on the sheet:
  //   2107086
endmodule

module Clockanalysisdecoding (
  input  Clock_Pulse,
  output clk_out,
  output sia,
  output ssa,
  output Sib,
  output ssb,
  output Mia,
  output Msa,
  output Sic,
  output ssc,
  output Mib,
  output Msb,
  output Mic,
  output Msc,
  output Sid,
  output ssd,
  output Mid,
  output Msd,
  output sie,
  output sse,
  output sif,
  output ssf,
  output Mie,
  output Mse,
  output sig,
  output ssg,
  output Mif,
  output Msf,
  output Mig,
  output Msg
);

  wire minutessecondscombination_1_mi0, minutessecondscombination_1_mi1, minutessecondscombination_1_mi2,
       minutessecondscombination_1_mi3, minutessecondscombination_1_ml0, minutessecondscombination_1_ml1,
       minutessecondscombination_1_ml2, minutessecondscombination_1_si0, minutessecondscombination_1_si1,
       minutessecondscombination_1_si2, minutessecondscombination_1_si3, minutessecondscombination_1_sl0,
       minutessecondscombination_1_sl1, minutessecondscombination_1_sl2;

  sevensegment_BCDto_dd79e25d sevensegment_bcdto_dd79e25d_1 (
    .in_1(1'b0), .in_2(minutessecondscombination_1_ml2), .in_4(minutessecondscombination_1_ml1),
    .D(minutessecondscombination_1_ml0), .a(Mia), .b(Mib), .c(Mic), .out_8(Mid), .e(Mie), .f(Mif), .g(Mig));
  minutessecondscombination minutessecondscombination_1 (
    .Clock_Pluse(Clock_Pulse), .ml2(minutessecondscombination_1_ml2), .ml1(minutessecondscombination_1_ml1),
    .ml0(minutessecondscombination_1_ml0), .mi3(minutessecondscombination_1_mi3),
    .mi2(minutessecondscombination_1_mi2), .mi1(minutessecondscombination_1_mi1),
    .mi0(minutessecondscombination_1_mi0), .si0(minutessecondscombination_1_si0), .clk_out(clk_out),
    .si1(minutessecondscombination_1_si1), .si2(minutessecondscombination_1_si2),
    .si3(minutessecondscombination_1_si3), .Sl0(minutessecondscombination_1_sl0),
    .sl1(minutessecondscombination_1_sl1), .sl2(minutessecondscombination_1_sl2));
  sevensegment_BCDto_dd79e25d sevensegment_bcdto_dd79e25d_2 (
    .in_1(minutessecondscombination_1_mi3), .in_2(minutessecondscombination_1_mi2),
    .in_4(minutessecondscombination_1_mi1), .D(minutessecondscombination_1_mi0), .a(Msa), .b(Msb), .c(Msc),
    .out_8(Msd), .e(Mse), .f(Msf), .g(Msg));
  sevensegment_BCDto_dd79e25d sevensegment_bcdto_dd79e25d_3 (
    .in_1(1'b0), .in_2(minutessecondscombination_1_sl2), .in_4(minutessecondscombination_1_sl1),
    .D(minutessecondscombination_1_sl0), .a(sia), .b(Sib), .c(Sic), .out_8(Sid), .e(sie), .f(sif), .g(sig));
  sevensegment_BCDto_dd79e25d sevensegment_bcdto_dd79e25d_4 (
    .in_1(minutessecondscombination_1_si3), .in_2(minutessecondscombination_1_si2),
    .in_4(minutessecondscombination_1_si1), .D(minutessecondscombination_1_si0), .a(ssa), .b(ssb), .c(ssc),
    .out_8(ssd), .e(sse), .f(ssf), .g(ssg));

  // Notes on the sheet:
  //   2107086
endmodule

module \new  (
  input  Clk_In_f31b25c5,
  output Q3,
  output Q2,
  output Q1,
  output Q0,
  output am_pm_b337f7e9
);

  wire and_1_out, and_2_out, and_3_out, and_4_out, button_1_out, undriven;

  T_Flip_Flop t_ff_1 (.reset(am_pm_b337f7e9), .preset(am_pm_b337f7e9));  // open: T, clk, Q, Qn
  T_Flip_Flop t_ff_2 (.clk(and_4_out), .reset(Q3), .preset(Q3));  // open: T, Q, Qn
  and and_1 (and_1_out, Q0, Q1, Q2);
  and and_2 (and_2_out, Q3, Q2);
  and and_3 (and_3_out, Q1, Q0);
  T_Flip_Flop t_ff_3 (.clk(Clk_In_f31b25c5), .T(and_3_out), .Q(Q2), .reset(and_4_out));  // open: Qn, preset
  and and_4 (and_4_out, Q2, Q3, Q0, undriven);
  T_Flip_Flop t_ff_4 (.clk(and_4_out), .reset(Q1), .preset(Q1));  // open: T, Q, Qn
  T_Flip_Flop t_ff_5 (.reset(Q0), .preset(Q0));  // open: T, clk, Q, Qn
  Button button_1 (.out(button_1_out));

  // Notes on the sheet:
  //   2107086
endmodule

module wrongnew (
  input  I3,
  input  I2,
  input  I1,
  input  I0,
  output QA0,
  output QB_448d706e,
  output QC0,
  output QD0,
  output QE0,
  output QF0,
  output QG0,
  output QG1,
  output QA1,
  output QB1,
  output QC1,
  output QD1,
  output QE1,
  output QF1
);

  wire and_1_out, and_2_out, and_3_out, and_4_out, and_5_out, and_6_out, and_7_out, and_8_out, and_9_out,
       and_10_out, and_11_out, and_12_out, not_1_out, not_2_out, not_3_out, not_4_out, or_1_out, or_2_out,
       or_3_out, or_4_out;

  not not_1 (not_1_out, I3);
  not not_2 (not_2_out, I2);
  not not_3 (not_3_out, I1);
  not not_4 (not_4_out, I0);
  and and_1 (and_1_out, I2, I0);
  and and_2 (and_2_out, not_2_out, not_4_out);
  and and_3 (and_3_out, I1, I0);
  and and_4 (and_4_out, not_3_out, not_4_out);
  or or_1 (or_1_out, I1, not_2_out);
  and and_5 (and_5_out, or_1_out, not_4_out);
  and and_6 (and_6_out, I0, not_3_out, I2);
  and and_7 (and_7_out, I1, not_2_out);
  or or_2 (or_2_out, I1, not_2_out);
  or or_3 (or_3_out, not_4_out, not_3_out);
  and and_8 (and_8_out, or_3_out, I2);
  and and_9 (and_9_out, not_4_out, not_3_out);
  or or_4 (or_4_out, not_4_out, not_3_out);
  and and_10 (and_10_out, or_4_out, I2);
  and and_11 (and_11_out, I1, not_2_out);
  and and_12 (and_12_out, not_2_out, not_3_out);
  or or_5 (QA0, and_1_out, and_2_out, I3, I1);
  or or_6 (QB_448d706e, and_3_out, and_4_out, not_2_out);
  or or_7 (QC0, I2, not_3_out, I0);
  or or_8 (QD0, and_5_out, and_6_out, and_7_out, I3);
  and and_13 (QE0, not_4_out, or_2_out);
  or or_9 (QF0, and_8_out, and_9_out, I3);
  or or_10 (QG0, and_10_out, and_11_out, I3);
  or or_11 (QA1, and_12_out, not_1_out);
  _7_Segment_Display u_7_segment_display_1 (
    .g(QG0), .f(QF0), .a(QA0), .b(QB_448d706e), .e(QE0), .d(QD0), .c(QC0));  // open: dp

  assign QB1 = 1'b1;
  assign QC1 = 1'b1;
  assign QD1 = QA1;
  assign QE1 = QA1;
  assign QF1 = QA1;
  assign QG1 = 1'b0;

  // Notes on the sheet:
  //   2107086
endmodule

module thikkortasi (
  input  I3,
  input  I2,
  input  I1,
  input  I0,
  output QA1,
  output QB1,
  output QC1,
  output QD1,
  output QE1,
  output QF1,
  output QG1,
  output QA0,
  output QB0,
  output QD0,
  output QC0,
  output QE0,
  output QF0,
  output QG0
);

  wire and_1_out, and_8_out, and_9_out, and_10_out, and_11_out, not_1_out, not_2_out, not_3_out, not_4_out,
       or_2_out, or_3_out, or_4_out, or_5_out, or_6_out, or_7_out, or_8_out, or_9_out, or_10_out, or_11_out,
       or_12_out, or_13_out, or_14_out, or_15_out, or_16_out;

  not not_1 (not_1_out, I3);
  not not_2 (not_2_out, I1);
  not not_3 (not_3_out, I0);
  not not_4 (not_4_out, I2);
  or or_1 (QA1, not_1_out, and_1_out);
  and and_1 (and_1_out, not_2_out, not_4_out);
  or or_2 (or_2_out, not_3_out, not_2_out, not_1_out);
  or or_3 (or_3_out, I0, I1, not_4_out, I3);
  or or_4 (or_4_out, not_3_out, I1, I2, I3);
  or or_5 (or_5_out, I0, not_2_out, not_4_out);
  and and_2 (QB0, or_5_out, or_6_out);
  or or_6 (or_6_out, not_3_out, I1, not_4_out);
  or or_7 (or_7_out, not_4_out, not_1_out);
  or or_8 (or_8_out, I0, not_2_out, I2, I3);
  or or_9 (or_9_out, I1, not_4_out, I3);
  or or_10 (or_10_out, not_4_out, not_1_out);
  or or_11 (or_11_out, not_3_out, not_2_out);
  or or_12 (or_12_out, not_2_out, I2, I3);
  or or_13 (or_13_out, not_3_out, I2, I3);
  or or_14 (or_14_out, not_2_out, not_1_out);
  or or_15 (or_15_out, not_3_out, not_2_out, not_4_out);
  and and_3 (QG0, or_14_out, or_15_out, or_16_out);
  or or_16 (or_16_out, I1, I2, I3);
  and and_4 (QA0, or_2_out, or_3_out, or_4_out);
  and and_5 (QC0, or_7_out, or_8_out);
  and and_6 (QE0, not_3_out, or_9_out);
  and and_7 (QF0, or_10_out, or_11_out, or_12_out, or_13_out);
  and and_8 (and_8_out, not_2_out, I2);
  and and_9 (and_9_out, I2, not_1_out);
  and and_10 (and_10_out, not_1_out, not_2_out);
  and and_11 (and_11_out, I1, not_4_out, I3);
  or or_17 (QD0, I0, and_11_out);
  _7_Segment_Display u_7_segment_display_1 (.g(QG0), .f(QF0), .a(QA0), .b(QB0), .e(QE0), .d(QD0), .c(QC0));  // open: dp

  assign QB1 = 1'b1;
  assign QC1 = 1'b1;
  assign QD1 = QA1;
  assign QE1 = QA1;
  assign QF1 = QA1;
  assign QG1 = 1'b0;

  // Notes on the sheet:
  //   2107086
endmodule

module simplify (
  input  I3,
  input  I2,
  input  I1,
  input  I0,
  output QA0,
  output QB0,
  output QANOT_89345d3a,
  output QC0,
  output QB1,
  output QC1,
  output QD1,
  output QENOT_3fae106c,
  output QD0,
  output QFNOT_432cf589,
  output QG1,
  output QE0,
  output QF0,
  output QG0
);

  wire and_1_out, and_2_out, and_3_out, and_4_out, and_5_out, and_6_out, and_7_out, and_8_out, and_9_out,
       and_10_out, and_11_out, and_12_out, and_13_out, and_14_out, and_15_out, and_16_out, and_17_out,
       and_18_out, and_19_out, and_20_out, and_21_out, and_22_out, and_23_out, and_24_out, and_25_out,
       and_26_out, and_27_out, and_28_out, and_29_out, and_30_out, and_31_out, and_32_out, and_33_out,
       and_34_out, and_35_out, not_1_out, not_2_out, not_3_out, not_4_out, not_5_out, not_6_out, not_7_out,
       not_8_out, not_9_out, not_10_out, not_11_out, not_12_out, not_13_out, not_14_out, not_15_out,
       not_16_out, not_17_out, not_18_out, not_19_out, not_20_out, not_21_out, not_22_out, not_23_out,
       not_24_out, not_25_out, not_26_out, not_27_out, not_28_out, not_29_out, not_30_out, not_31_out,
       not_32_out, not_33_out, not_34_out, not_35_out, not_36_out, not_37_out, not_38_out, not_39_out,
       not_40_out, not_41_out, not_42_out, or_1_out, or_3_out, or_4_out, or_6_out, or_8_out, or_9_out,
       or_10_out, or_12_out, or_13_out, or_14_out, or_15_out, or_16_out, or_17_out, or_18_out;

  not not_1 (not_1_out, I2);
  not not_2 (not_2_out, I0);
  not not_3 (not_3_out, I3);
  not not_4 (not_4_out, I1);
  not not_5 (not_5_out, I1);
  not not_6 (not_6_out, I0);
  not not_7 (not_7_out, I3);
  not not_8 (not_8_out, I1);
  not not_9 (not_9_out, I3);
  not not_10 (not_10_out, I2);
  not not_11 (not_11_out, I3);
  not not_12 (not_12_out, I2);
  not not_13 (not_13_out, I2);
  not not_14 (not_14_out, I0);
  not not_15 (not_15_out, I0);
  not not_16 (not_16_out, I3);
  not not_17 (not_17_out, I1);
  not not_18 (not_18_out, I3);
  not not_19 (not_19_out, I3);
  not not_20 (not_20_out, I2);
  and and_1 (and_1_out, not_1_out, not_2_out);
  and and_2 (and_2_out, not_3_out, I1);
  and and_3 (and_3_out, I2, I0);
  and and_4 (and_4_out, I3, not_4_out);
  not not_21 (not_21_out, I2);
  and and_5 (and_5_out, not_5_out, not_6_out);
  and and_6 (and_6_out, not_7_out, not_8_out);
  and and_7 (and_7_out, not_9_out, I2);
  and and_8 (and_8_out, I3, not_10_out);
  not not_22 (not_22_out, I2);
  not not_23 (not_23_out, I0);
  and and_9 (and_9_out, not_11_out, not_12_out);
  not not_24 (not_24_out, I1);
  and and_10 (and_10_out, not_13_out, not_14_out);
  and and_11 (and_11_out, I1, not_15_out);
  not not_25 (not_25_out, I0);
  and and_12 (and_12_out, not_16_out, not_17_out);
  not not_26 (not_26_out, I0);
  and and_13 (and_13_out, not_18_out, I2);
  not not_27 (not_27_out, I1);
  not not_28 (not_28_out, I3);
  not not_29 (not_29_out, I2);
  not not_30 (not_30_out, I2);
  and and_14 (and_14_out, not_19_out, not_20_out);
  not not_31 (not_31_out, I1);
  not not_32 (not_32_out, I0);
  not not_33 (not_33_out, I1);
  or or_1 (or_1_out, and_1_out, and_2_out);
  or or_2 (QA0, or_1_out, or_3_out);
  or or_3 (or_3_out, and_3_out, and_4_out);
  or or_4 (or_4_out, not_21_out, and_5_out);
  or or_5 (QB0, or_4_out, and_15_out);
  and and_15 (and_15_out, I1, I0);
  or or_6 (or_6_out, and_6_out, I0);
  or or_7 (QC0, or_6_out, or_8_out);
  or or_8 (or_8_out, and_7_out, and_8_out);
  and and_16 (and_16_out, not_22_out, not_23_out);
  or or_9 (or_9_out, and_16_out, and_17_out);
  and and_17 (and_17_out, and_9_out, I1);
  and and_18 (and_18_out, I1, not_34_out);
  not not_34 (not_34_out, I0);
  and and_19 (and_19_out, I2, not_24_out);
  and and_20 (and_20_out, and_19_out, I0);
  and and_21 (and_21_out, I3, not_35_out);
  not not_35 (not_35_out, I1);
  or or_10 (or_10_out, and_10_out, and_11_out);
  or or_11 (QE0, or_10_out, and_22_out);
  and and_22 (and_22_out, I3, not_25_out);
  and and_23 (and_23_out, and_12_out, not_26_out);
  or or_12 (or_12_out, and_23_out, and_24_out);
  and and_24 (and_24_out, and_13_out, not_27_out);
  and and_25 (and_25_out, not_28_out, I2);
  and and_26 (and_26_out, and_25_out, not_36_out);
  not not_36 (not_36_out, I0);
  and and_27 (and_27_out, I3, not_29_out);
  and and_28 (and_28_out, and_27_out, not_37_out);
  not not_37 (not_37_out, I1);
  and and_29 (and_29_out, I3, not_30_out);
  and and_30 (and_30_out, and_29_out, not_38_out);
  not not_38 (not_38_out, I0);
  and and_31 (and_31_out, and_14_out, I1);
  or or_13 (or_13_out, and_31_out, and_32_out);
  and and_32 (and_32_out, I2, not_31_out);
  and and_33 (and_33_out, I2, not_32_out);
  or or_14 (or_14_out, and_33_out, and_34_out);
  and and_34 (and_34_out, I3, not_33_out);
  or or_15 (or_15_out, or_9_out, and_18_out);
  or or_16 (or_16_out, and_20_out, and_21_out);
  or or_17 (or_17_out, or_12_out, and_26_out);
  or or_18 (or_18_out, and_28_out, and_30_out);
  or or_19 (QG0, or_13_out, or_14_out);
  or or_20 (QD0, or_15_out, or_16_out);
  or or_21 (QF0, or_17_out, or_18_out);
  not not_39 (not_39_out, I3);
  not not_40 (not_40_out, I2);
  not not_41 (not_41_out, I1);
  not not_42 (not_42_out, I0);
  or or_22 (QANOT_89345d3a, not_39_out, and_35_out);
  and and_35 (and_35_out, not_41_out, not_40_out);

  assign QB1 = 1'b1;
  assign QC1 = 1'b1;
  assign QD1 = QANOT_89345d3a;
  assign QENOT_3fae106c = QANOT_89345d3a;
  assign QFNOT_432cf589 = QANOT_89345d3a;
  assign QG1 = 1'b0;

  // Notes on the sheet:
  //   2107086
endmodule

module L_1t012counter_1b653834 (
  input  Clk_In_f31b25c5,
  output Q3,
  output Q2,
  output Q1,
  output Q0,
  output am_pm_b337f7e9
);

  wire and_1_out, and_2_out, and_3_out, and_4_out, button_1_out, undriven;

  T_Flip_Flop t_ff_1 (.reset(am_pm_b337f7e9), .preset(am_pm_b337f7e9));  // open: T, clk, Q, Qn
  T_Flip_Flop t_ff_2 (.clk(and_4_out), .reset(Q3), .preset(Q3));  // open: T, Q, Qn
  and and_1 (and_1_out, Q0, Q1, Q2);
  and and_2 (and_2_out, Q3, Q2);
  and and_3 (and_3_out, Q1, Q0);
  T_Flip_Flop t_ff_3 (.clk(Clk_In_f31b25c5), .T(and_3_out), .Q(Q2), .reset(and_4_out));  // open: Qn, preset
  and and_4 (and_4_out, Q2, Q3, Q0, undriven);
  T_Flip_Flop t_ff_4 (.clk(and_4_out), .reset(Q1), .preset(Q1));  // open: T, Q, Qn
  T_Flip_Flop t_ff_5 (.reset(Q0), .preset(Q0));  // open: T, clk, Q, Qn
  Button button_1 (.out(button_1_out));

  // Notes on the sheet:
  //   2107086
endmodule
